# Fritzing sketch dht22 (saved by Fritzing 0.9.4)
circuit board: 8.46667cm x 5.64444cm
breadboards: 1

parts:
  Part1 = Arduino Nano (Rev3.0)
  U1 = mystery part, 3 pins [chip_label=AM2302]

nets:
  N1: Part1.GND, U1.pin3
  N2: Part1.D2, U1.pin2
  N3: Part1.5V, U1.pin1
