# Fritzing sketch potentiometer_diagram (saved by Fritzing 0.9.4)
circuit board: 8.46667cm x 5.64444cm
breadboards: 1

parts:
  Part1 = Arduino Nano (Rev3.0)
  R1 = TRIMPOT [package=3362u-2]

nets:
  N1: Part1.GND, R1.CW
  N2: Part1.A0, R1.WIPER
  N3: Part1.3V3, R1.CCW
